# Fritzing sketch Hotkeypad (saved by Fritzing 0.9.3b)
breadboards: 1

parts:
  C1 = Capacitor Polarized [package=panasonic_e]
  S1 = SWITCH-MOMENTARY-2 [package=tactile_switch_tall]
  S2 = SWITCH-MOMENTARY-2 [package=tactile_switch_tall]
  S3 = SWITCH-MOMENTARY-2 [package=tactile_switch_tall]
  S4 = SWITCH-MOMENTARY-2 [package=tactile_switch_tall]
  S5 = SWITCH-MOMENTARY-2 [package=tactile_switch_tall]
  S6 = SWITCH-MOMENTARY-2 [package=tactile_switch_tall]
  S7 = SWITCH-MOMENTARY-2 [package=tactile_switch_tall]
  S8 = SWITCH-MOMENTARY-2 [package=tactile_switch_tall]
  S11 = SWITCH-MOMENTARY-2 [package=tactile_switch_tall]
  S9 = SWITCH-MOMENTARY-2 [package=tactile_switch_tall]
  S10 = SWITCH-MOMENTARY-2 [package=tactile_switch_tall]
  S12 = SWITCH-MOMENTARY-2 [package=tactile_switch_tall]
  S15 = SWITCH-MOMENTARY-2 [package=tactile_switch_tall]
  S13 = SWITCH-MOMENTARY-2 [package=tactile_switch_tall]
  S14 = SWITCH-MOMENTARY-2 [package=tactile_switch_tall]
  S16 = SWITCH-MOMENTARY-2 [package=tactile_switch_tall]
  R5 = 1000 Ω Resistor [package="0805 [SMD]"]
  R8 = 1000 Ω Resistor [package="0805 [SMD]"]
  R1 = 100 Ω Resistor [package="0805 [SMD]"]
  R2 = 470 Ω Resistor [package="0805 [SMD]"]
  R3 = 2200 Ω Resistor [package="0805 [SMD]"]
  R4 = 22000 Ω Resistor [package="0805 [SMD]"]
  R7 = 4700 Ω Resistor [package="0805 [SMD]"]
  R6 = 6800 Ω Resistor [package="0805 [SMD]"]

nets:
  GND: C1.+, R5.Pin_1
  A0: C1.-, S15.1, S13.1, S14.1, S16.1, R8.Pin_0
  N1: S1.2, S3.2, S5.2, S6.2, S11.2, S9.2, S15.2, S13.2, R1.Pin_0, R2.Pin_1, R3.Pin_0, R4.Pin_1
  N2: S1.1, S2.1, S3.1, S4.1, R5.Pin_0, R6.Pin_1
  N3: S2.2, S7.2, S10.2, S14.2, R2.Pin_0, R3.Pin_1
  N4: S4.2, S8.2, S12.2, S16.2, R4.Pin_0
  N5: S5.1, S6.1, S7.1, S8.1
  N6: S11.1, S9.1, S10.1, S12.1, R8.Pin_1, R7.Pin_0
  5V: R1.Pin_1
  N7: R7.Pin_1, R6.Pin_0

custom parts:
  1000 Ω Resistor: A generic resistor
  100 Ω Resistor: A generic resistor
  470 Ω Resistor: A generic resistor
  2200 Ω Resistor: A generic resistor
  22000 Ω Resistor: A generic resistor
  4700 Ω Resistor: A generic resistor
  6800 Ω Resistor: A generic resistor
